# Fritzing sketch NetPeek (saved by Fritzing 0.7.5b)
stripboards: 1

parts:
  R1 = Resistor [tolerance=±5% resistance=6.8k package=THT]
  Q1 = NPN-Transistor [package="TO92 [THT]"]
  LED1 = LED - 5mm [color="Red (633nm)" package="5 mm [THT]"]
  R2 = Resistor [tolerance=±5% resistance=82 package=THT]
  R3 = Resistor [tolerance=±5% resistance=82 package=THT]
  LED2 = LED - 5mm [color="Red (633nm)" package="5 mm [THT]"]
  Arduino_Ethernet_Shield1 = Arduino Ethernet Shield

nets:
  N1: R1.Pin_0, Arduino_Ethernet_Shield1.D8
  N2: R1.Pin_1, Q1.B
  GND: Q1.E, Arduino_Ethernet_Shield1.GND
  N3: Q1.C, LED1.cathode, LED2.cathode
  N4: LED1.anode, R3.Pin_1
  5V: R2.Pin_0, R3.Pin_0, Arduino_Ethernet_Shield1.+5V
  N5: R2.Pin_1, LED2.anode

notes:
  3.5V 18mA
  hFE=50
  0.7mA
